// Logisim project AK projekt 1.circ as structural Verilog: 5 circuits, main circuit pełny 74194
module \pełny_74194  (
  input  SR,
  input  A,
  input  B,
  input  C,
  input  D,
  input  SL,
  input  S0,
  input  S1,
  input  CLR,
  output QA,
  output QB,
  output QC,
  output QD
);

  wire and_1_out, and_2_out, and_3_out, and_4_out, and_5_out, and_6_out, and_7_out, and_8_out, and_9_out,
       and_10_out, and_11_out, and_12_out, and_13_out, clock_1_out, nor_1_out, nor_2_out, nor_3_out,
       nor_4_out, nor_5_out, nor_6_out, not_1_out, not_2_out, not_3_out, not_4_out, not_5_out, not_6_out,
       not_7_out, not_8_out, not_9_out, not_10_out, not_11_out;

  Clock clock_1 (.out(clock_1_out));
  not not_1 (not_1_out, S0);
  not not_2 (not_2_out, S1);
  nor nor_1 (nor_1_out, not_1_out, not_2_out);
  and and_1 (and_1_out, not_2_out, not_1_out);
  not not_3 (not_3_out, CLR);
  and and_2 (and_2_out, SR, not_2_out);
  nor nor_2 (nor_2_out, and_1_out, clock_1_out);
  and and_3 (and_3_out, not_1_out, QB);
  and and_4 (and_4_out, nor_1_out, A);
  nor nor_3 (nor_3_out, and_2_out, and_4_out, and_3_out);
  not not_4 (not_4_out, nor_3_out);
  not not_5 (not_5_out, nor_2_out);
  S_R_Flip_Flop s_r_ff_1 (
    .S(not_4_out), .clk(not_5_out), .R(nor_3_out), .Q(QA), .reset(not_3_out));  // open: Qn, preset, en
  and and_5 (and_5_out, QA, not_2_out);
  and and_6 (and_6_out, nor_1_out, B);
  nor nor_4 (nor_4_out, and_5_out, and_6_out, and_7_out);
  and and_7 (and_7_out, not_1_out, QC);
  not not_6 (not_6_out, nor_4_out);
  not not_7 (not_7_out, nor_2_out);
  S_R_Flip_Flop s_r_ff_2 (
    .S(not_6_out), .clk(not_7_out), .R(nor_4_out), .Q(QB), .reset(not_3_out));  // open: Qn, preset, en
  and and_8 (and_8_out, QB, not_2_out);
  and and_9 (and_9_out, nor_1_out, C);
  nor nor_5 (nor_5_out, and_8_out, and_9_out, and_10_out);
  and and_10 (and_10_out, not_1_out, QD);
  not not_8 (not_8_out, nor_5_out);
  not not_9 (not_9_out, nor_2_out);
  S_R_Flip_Flop s_r_ff_3 (
    .S(not_8_out), .clk(not_9_out), .R(nor_5_out), .Q(QC), .reset(not_3_out));  // open: Qn, preset, en
  and and_11 (and_11_out, QC, not_2_out);
  and and_12 (and_12_out, nor_1_out, D);
  nor nor_6 (nor_6_out, and_11_out, and_12_out, and_13_out);
  not not_10 (not_10_out, nor_6_out);
  not not_11 (not_11_out, nor_2_out);
  and and_13 (and_13_out, not_1_out, SL);
  S_R_Flip_Flop s_r_ff_4 (
    .S(not_10_out), .clk(not_11_out), .R(nor_6_out), .Q(QD), .reset(not_3_out));  // open: Qn, preset, en

  // Notes on the sheet:
  //   CLK
endmodule

module uproszczony_74194 (
  input  S0,
  input  A,
  input  B,
  input  C,
  input  D,
  input  S1,
  input  LIN,
  input  CLR,
  output QA,
  output QB,
  output QC,
  output QD
);

  wire and_1_out, clock_1_out;

  Clock clock_1 (.out(clock_1_out));
  and and_1 (and_1_out, S1, S0);
  Shift_Register #(.length(4)) shift_register_1 (
    .shift(S1), .in(LIN), .clk(clock_1_out), .load(and_1_out), .clr(CLR), .d0(D), .q0(QD), .d1(C), .q1(QC),
    .d2(B), .q2(QB), .d3(A), .q3(QA));  // open: out

  // Notes on the sheet:
  //   CLK
endmodule

module uproszczony_a (
  input  S0,
  output QA,
  output QB,
  output QC,
  output QD
);

  wire and_1_out, clock_1_out, not_1_out;

  Clock clock_1 (.out(clock_1_out));
  and and_1 (and_1_out, 1'b1, S0);
  Shift_Register #(.length(4)) shift_register_1 (
    .shift(1'b1), .in(QA), .clk(clock_1_out), .load(and_1_out), .clr(not_1_out), .d0(1'b1), .q0(QD),
    .d1(1'b0), .q1(QC), .d2(1'b0), .q2(QB), .d3(1'b0), .q3(QA));  // open: out
  not not_1 (not_1_out, 1'b1);

  // Notes on the sheet:
  //   reset
  //   CLK
endmodule

module uproszczony_b (
  output QA,
  output QB,
  output QC,
  output QD
);

  wire and_1_out, clock_1_out, nand_1_out, not_1_out;

  Clock clock_1 (.out(clock_1_out));
  and and_1 (and_1_out, 1'b1, 1'b0);
  not not_1 (not_1_out, 1'b1);
  Shift_Register #(.length(4)) shift_register_1 (
    .shift(1'b1), .in(nand_1_out), .clk(clock_1_out), .load(and_1_out), .clr(not_1_out), .d0(1'b0), .q0(QD),
    .d1(1'b0), .q1(QC), .d2(1'b0), .q2(QB), .d3(1'b0), .q3(QA));  // open: out
  nand nand_1 (nand_1_out, QB, QC, QD);

  // Notes on the sheet:
  //   CLK
endmodule

module uproszczony_c (
  input  S1,
  output QA,
  output QB,
  output QC,
  output QD
);

  wire and_1_out, clock_1_out, not_1_out;

  Clock clock_1 (.out(clock_1_out));
  and and_1 (and_1_out, S1, 1'b0);
  Shift_Register #(.length(4)) shift_register_1 (
    .shift(S1), .in(not_1_out), .clk(clock_1_out), .load(and_1_out), .d0(1'b0), .q0(QD), .d1(1'b0), .q1(QC),
    .d2(1'b0), .q2(QB), .d3(1'b0), .q3(QA));  // open: out, clr
  not not_1 (not_1_out, QA);

  // Notes on the sheet:
  //   RESET
  //   CLK
endmodule
