// Logisim project AK projekt 4.circ as structural Verilog: 4 circuits, main circuit D Flip-Flop master-slave
module \Układ_pierwotny  (
  input  X,
  output Z
);

  wire and_1_out, and_2_out, and_3_out, clock_1_out, d_ff_1_q, d_ff_1_qn, d_ff_2_q, or_1_out, or_2_out;

  and and_1 (and_1_out, d_ff_1_qn, X);
  and and_2 (and_2_out, X, d_ff_2_q);
  and and_3 (and_3_out, X, d_ff_1_q);
  or or_1 (or_1_out, and_1_out, and_2_out);
  or or_2 (or_2_out, and_2_out, and_3_out);
  Clock clock_1 (.out(clock_1_out));
  D_Flip_Flop d_ff_1 (.clk(clock_1_out), .D(or_1_out), .Q(d_ff_1_q), .Qn(d_ff_1_qn));  // open: preset, en, reset
  D_Flip_Flop d_ff_2 (.clk(clock_1_out), .D(or_2_out), .Q(d_ff_2_q));  // open: Qn, preset, en, reset
  and and_4 (Z, d_ff_1_q, d_ff_2_q);
endmodule

module D_Flip_Flop_master_slave (
  input  D,
  output Q,
  output Q_prime
);

  wire clock_1_out, nand_1_out, nand_2_out, nand_3_out, nand_4_out, nand_5_out, nand_6_out, nor_1_out;

  Clock clock_1 (.out(clock_1_out));
  nor nor_1 (nor_1_out, clock_1_out, clock_1_out);
  nand nand_1 (nand_1_out, nand_2_out, nand_4_out);
  nand nand_2 (nand_2_out, D, nor_1_out);
  nand nand_3 (nand_3_out, nand_2_out, nor_1_out);
  nand nand_4 (nand_4_out, nand_1_out, nand_3_out);
  nand nand_5 (nand_5_out, nand_1_out, clock_1_out);
  nand nand_6 (nand_6_out, nand_5_out, clock_1_out);
  nand nand_7 (Q, nand_5_out, Q_prime);
  nand nand_8 (Q_prime, Q, nand_6_out);
endmodule

module Uklad_NAND (
  input  X,
  output Z
);

  wire clock_1_out, nand_1_out, nand_2_out, nand_3_out, nand_4_out, nand_5_out, nand_6_out, nand_7_out,
       nand_8_out, nand_9_out, nand_10_out, nand_11_out, nand_12_out, nand_13_out, nand_14_out, nand_15_out,
       nand_16_out, nand_17_out, nand_18_out, nand_19_out, nand_20_out, nand_21_out, nand_22_out;

  Clock clock_1 (.out(clock_1_out));
  nand nand_1 (nand_1_out, X, nand_17_out);
  nand nand_2 (nand_2_out, X, nand_21_out);
  nand nand_3 (nand_3_out, X, nand_15_out);
  nand nand_4 (nand_4_out, nand_1_out, nand_2_out);
  nand nand_5 (nand_5_out, nand_2_out, nand_3_out);
  nand nand_6 (nand_6_out, X, clock_1_out);
  nand nand_7 (nand_7_out, nand_4_out, nand_6_out);
  nand nand_8 (nand_8_out, nand_7_out, nand_6_out);
  nand nand_9 (nand_9_out, nand_5_out, nand_6_out);
  nand nand_10 (nand_10_out, nand_9_out, nand_6_out);
  nand nand_11 (nand_11_out, nand_7_out, nand_12_out);
  nand nand_12 (nand_12_out, nand_11_out, nand_8_out);
  nand nand_13 (nand_13_out, nand_9_out, nand_14_out);
  nand nand_14 (nand_14_out, nand_13_out, nand_10_out);
  nand nand_15 (nand_15_out, nand_16_out, nand_17_out);
  nand nand_16 (nand_16_out, nand_11_out, clock_1_out);
  nand nand_17 (nand_17_out, nand_15_out, nand_18_out);
  nand nand_18 (nand_18_out, nand_16_out, clock_1_out);
  nand nand_19 (nand_19_out, nand_13_out, clock_1_out);
  nand nand_20 (nand_20_out, nand_19_out, clock_1_out);
  nand nand_21 (nand_21_out, nand_19_out, nand_22_out);
  nand nand_22 (nand_22_out, nand_21_out, nand_20_out);
  nor nor_1 (Z, nand_17_out, nand_22_out);

  // Notes on the sheet:
  //   D
  //   D
  //   Q
  //   Q'
  //   Q
  //   Q'
endmodule

module Uklad_JK (
  input  X,
  input  X_2,
  output Z,
  output Z_2
);

  wire and_1_out, and_2_out, and_3_out, and_4_out, and_5_out, and_6_out, and_7_out, and_8_out, clock_1_out,
       clock_2_out, d_ff_1_q, d_ff_1_qn, d_ff_2_q, j_k_ff_1_q, j_k_ff_1_qn, j_k_ff_2_q, not_1_out, not_2_out,
       not_3_out, not_4_out, not_5_out, not_6_out, or_1_out, or_2_out;

  and and_1 (and_1_out, j_k_ff_1_qn, X);
  and and_2 (and_2_out, X, j_k_ff_2_q);
  and and_3 (and_3_out, X, j_k_ff_1_q);
  and and_4 (and_4_out, d_ff_1_qn, X_2);
  and and_5 (and_5_out, X_2, d_ff_2_q);
  and and_6 (and_6_out, X_2, d_ff_1_q);
  not not_1 (not_1_out, and_1_out);
  and and_7 (and_7_out, not_1_out, not_2_out);
  not not_2 (not_2_out, and_2_out);
  not not_3 (not_3_out, and_2_out);
  and and_8 (and_8_out, not_3_out, not_4_out);
  not not_4 (not_4_out, and_3_out);
  or or_1 (or_1_out, and_4_out, and_5_out);
  or or_2 (or_2_out, and_5_out, and_6_out);
  Clock clock_1 (.out(clock_1_out));
  not not_5 (not_5_out, and_7_out);
  not not_6 (not_6_out, and_8_out);
  Clock clock_2 (.out(clock_2_out));
  D_Flip_Flop d_ff_1 (.clk(clock_2_out), .D(or_1_out), .Q(d_ff_1_q), .Qn(d_ff_1_qn));  // open: preset, en, reset
  D_Flip_Flop d_ff_2 (.clk(clock_2_out), .D(or_2_out), .Q(d_ff_2_q));  // open: Qn, preset, en, reset
  J_K_Flip_Flop j_k_ff_1 (
    .J(not_5_out), .clk(clock_1_out), .K(and_7_out), .Q(j_k_ff_1_q), .Qn(j_k_ff_1_qn));  // open: preset, en, reset
  J_K_Flip_Flop j_k_ff_2 (
    .J(not_6_out), .clk(clock_1_out), .K(and_8_out), .Q(j_k_ff_2_q));  // open: Qn, preset, en, reset
  and and_9 (Z, j_k_ff_1_q, j_k_ff_2_q);
  and and_10 (Z_2, d_ff_1_q, d_ff_2_q);

  // Notes on the sheet:
  //   Układ zmodyfikowany
  //   Układ pierwotny dla porównania
endmodule
