// Logisim project AK projekt 5.circ as structural Verilog: 2 circuits, main circuit Moore'a zsyntezowany
module Moore_a_zsyntezowany (
  input  X,
  output Z1,
  output Z2
);

  wire and_1_out, and_2_out, clk_out, d_ff_1_q, d_ff_1_qn, d_ff_2_q, d_ff_2_qn, not_1_out, or_1_out;

  and and_1 (and_1_out, d_ff_1_q, not_1_out);
  not not_1 (not_1_out, X);
  and and_2 (and_2_out, d_ff_1_qn, X);
  or or_1 (or_1_out, and_1_out, and_2_out);
  Clock clk (.out(clk_out));
  D_Flip_Flop d_ff_1 (.clk(clk_out), .D(or_1_out), .Q(d_ff_1_q), .Qn(d_ff_1_qn));  // open: preset, en, reset
  D_Flip_Flop d_ff_2 (.clk(clk_out), .D(d_ff_1_q), .Q(d_ff_2_q), .Qn(d_ff_2_qn));  // open: preset, en, reset
  and and_3 (Z1, d_ff_1_q, d_ff_2_qn);
  and and_4 (Z2, d_ff_1_qn, d_ff_2_q);
endmodule

module Mealy_ego_zsyntezowany (
  input  X,
  output Z1,
  output Z2
);

  wire clk_out, j_k_ff_1_q, j_k_ff_1_qn;

  J_K_Flip_Flop j_k_ff_1 (.J(X), .clk(clk_out), .K(X), .Q(j_k_ff_1_q), .Qn(j_k_ff_1_qn));  // open: preset, en, reset
  Clock clk (.out(clk_out));
  and and_1 (Z1, X, j_k_ff_1_q);
  and and_2 (Z2, j_k_ff_1_qn, X);
endmodule
